# Fritzing sketch Schematic (saved by Fritzing 0.9.3b)
breadboards: 1

parts:
  ESP32_-_Back1 = ESP32 - CAM
  J1 = Basic Servo
  Part1 = XBee USB Mini Adapter
  PIR1 = PIR sensor
  J2 = Piezo Speaker
  SW-1 = Vibration sensor module
  Part2 = KY-037 High Sensitivity Sound Detection Module [package="Breakout board"]

nets:
  N1: ESP32_-_Back1.GPIO2, J1.pulse
  N2: ESP32_-_Back1.GPIO14, Part2.D0
  5V: ESP32_-_Back1.GPIO15, ESP32_-_Back1.5V, J1.vcc, Part1.5V, PIR1.VDD, J2.pin2, SW-1.vcc, Part2.+
  N3: ESP32_-_Back1.GPIO13, PIR1.SIG
  N4: ESP32_-_Back1.GPIO12, SW-1.Ground
  GND: ESP32_-_Back1.GND#7, J1.gnd, Part1.GND, PIR1.GND, J2.pin1, SW-1.Digital_output, Part2.G
  N5: ESP32_-_Back1.GPIO3_/_RX, Part1.RXD
  N6: ESP32_-_Back1.GPIO1_/_TX, Part1.TXD

custom parts:
  ESP32 - CAM: The ESP32-CAM has a very competitive small-size camera module that can operate independently as a minimum system with a footprint of only 27*40.5*4.5mm and a deep sleep current of up to 6mA.
  Vibration sensor module: Single-roller type full induction trigger switch. When no vibration or tilt, the product is ON conduction state, and in the steady state, when a vibration or tilt, the switch will be rendered instantly disconnect the conductive resistance increases, generating a current pulse signal, thereby triggering circuit. The default state of the swith is close Digital output Supply voltage:3.3V-5V On-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
  KY-037 High Sensitivity Sound Detection Module: KY-037 high sensitivity sound detection module is an analog/digital sensor that uses a condenser microphone to observe changes in environment noise.
